// Digital circuit 1x17_SRAM.dig as structural Verilog
module _1x17_SRAM (
  input  RS1,
  input  RS2,
  input  WS,
  input  [16:0] WD_16_0,
  input  Clock,
  output [16:0] RD1,
  output [16:0] RD2
);

  _1x1_SRAM _1x1_sram_1 (.RS1(RS1), .RS2(RS2), .WD(WD_16_0[0]), .WS(WS), .Clock(Clock), .RD1(RD1[0]), .RD2(RD2[0]));
  _1x1_SRAM _1x1_sram_2 (.RS1(RS1), .RS2(RS2), .WD(WD_16_0[5]), .WS(WS), .Clock(Clock), .RD1(RD1[5]), .RD2(RD2[5]));
  _1x1_SRAM _1x1_sram_3 (.RS1(RS1), .RS2(RS2), .WD(WD_16_0[9]), .WS(WS), .Clock(Clock), .RD1(RD1[9]), .RD2(RD2[9]));
  _1x1_SRAM _1x1_sram_4 (.RS1(RS1), .RS2(RS2), .WD(WD_16_0[13]), .WS(WS), .Clock(Clock), .RD1(RD1[13]), .RD2(RD2[13]));
  _1x1_SRAM _1x1_sram_5 (.RS1(RS1), .RS2(RS2), .WD(WD_16_0[1]), .WS(WS), .Clock(Clock), .RD1(RD1[1]), .RD2(RD2[1]));
  _1x1_SRAM _1x1_sram_6 (.RS1(RS1), .RS2(RS2), .WD(WD_16_0[14]), .WS(WS), .Clock(Clock), .RD1(RD1[14]), .RD2(RD2[14]));
  _1x1_SRAM _1x1_sram_7 (.RS1(RS1), .RS2(RS2), .WD(WD_16_0[6]), .WS(WS), .Clock(Clock), .RD1(RD1[6]), .RD2(RD2[6]));
  _1x1_SRAM _1x1_sram_8 (.RS1(RS1), .RS2(RS2), .WD(WD_16_0[10]), .WS(WS), .Clock(Clock), .RD1(RD1[10]), .RD2(RD2[10]));
  _1x1_SRAM _1x1_sram_9 (.RS1(RS1), .RS2(RS2), .WD(WD_16_0[2]), .WS(WS), .Clock(Clock), .RD1(RD1[2]), .RD2(RD2[2]));
  _1x1_SRAM _1x1_sram_10 (.RS1(RS1), .RS2(RS2), .WD(WD_16_0[15]), .WS(WS), .Clock(Clock), .RD1(RD1[15]), .RD2(RD2[15]));
  _1x1_SRAM _1x1_sram_11 (.RS1(RS1), .RS2(RS2), .WD(WD_16_0[7]), .WS(WS), .Clock(Clock), .RD1(RD1[7]), .RD2(RD2[7]));
  _1x1_SRAM _1x1_sram_12 (.RS1(RS1), .RS2(RS2), .WD(WD_16_0[11]), .WS(WS), .Clock(Clock), .RD1(RD1[11]), .RD2(RD2[11]));
  _1x1_SRAM _1x1_sram_13 (.RS1(RS1), .RS2(RS2), .WD(WD_16_0[3]), .WS(WS), .Clock(Clock), .RD1(RD1[3]), .RD2(RD2[3]));
  _1x1_SRAM _1x1_sram_14 (.RS1(RS1), .RS2(RS2), .WD(WD_16_0[16]), .WS(WS), .Clock(Clock), .RD1(RD1[16]), .RD2(RD2[16]));
  _1x1_SRAM _1x1_sram_15 (.RS1(RS1), .RS2(RS2), .WD(WD_16_0[8]), .WS(WS), .Clock(Clock), .RD1(RD1[8]), .RD2(RD2[8]));
  _1x1_SRAM _1x1_sram_16 (.RS1(RS1), .RS2(RS2), .WD(WD_16_0[12]), .WS(WS), .Clock(Clock), .RD1(RD1[12]), .RD2(RD2[12]));
  _1x1_SRAM _1x1_sram_17 (.RS1(RS1), .RS2(RS2), .WD(WD_16_0[4]), .WS(WS), .Clock(Clock), .RD1(RD1[4]), .RD2(RD2[4]));

  // Other names for the same wires on the sheet: clk = Clock; RD1_0 = RD1[0]; RD1_1 = RD1[1]; RD1_2 = RD1[2];
  //   RD1_3 = RD1[3]; RD1_4 = RD1[4]; RD1_5 = RD1[5]; RD1_6 = RD1[6]; RD1_7 = RD1[7]; RD1_8 = RD1[8]; RD1_9 = RD1[9];
  //   RD1_10 = RD1[10]; RD1_11 = RD1[11]; RD1_12 = RD1[12]; RD1_13 = RD1[13]; RD1_14 = RD1[14]; RD1_15 = RD1[15];
  //   RD1_16 = RD1[16]; RD2_0 = RD2[0]; RD2_1 = RD2[1]; RD2_2 = RD2[2]; RD2_3 = RD2[3]; RD2_4 = RD2[4];
  //   RD2_5 = RD2[5]; RD2_6 = RD2[6]; RD2_7 = RD2[7]; RD2_8 = RD2[8]; RD2_9 = RD2[9]; RD2_10 = RD2[10];
  //   RD2_11 = RD2[11]; RD2_12 = RD2[12]; RD2_13 = RD2[13]; RD2_14 = RD2[14]; RD2_15 = RD2[15]; RD2_16 = RD2[16];
  //   wd0 = WD_16_0[0]; wd1 = WD_16_0[1]; wd2 = WD_16_0[2]; wd3 = WD_16_0[3]; wd4 = WD_16_0[4]; wd5 = WD_16_0[5];
  //   wd6 = WD_16_0[6]; wd7 = WD_16_0[7]; wd8 = WD_16_0[8]; wd9 = WD_16_0[9]; wd10 = WD_16_0[10]; wd11 = WD_16_0[11];
  //   wd12 = WD_16_0[12]; wd13 = WD_16_0[13]; wd14 = WD_16_0[14]; wd15 = WD_16_0[15]; wd16 = WD_16_0[16]
endmodule
