// Digital circuit 3_Bit_Control_Unit.dig as structural Verilog
module _3_Bit_Control_Unit (
  input  [3:0] Opcode_3_0,
  input  ZF,
  input  SF,
  output [1:0] Op_1_0,
  output REG_EN,
  output Imm_Sel,
  output Jmp_Sel
);

  wire and_1_out, and_3_out, and_4_out, and_5_out, not_1_out, not_2_out, not_3_out, not_4_out, not_5_out,
       not_6_out, not_7_out, not_8_out, not_9_out, or_1_out;

  not not_1 (not_1_out, Opcode_3_0[2]);
  not not_2 (not_2_out, Opcode_3_0[3]);
  not not_3 (not_3_out, Opcode_3_0[3]);
  not not_4 (not_4_out, Opcode_3_0[2]);
  not not_5 (not_5_out, Opcode_3_0[0]);
  not not_6 (not_6_out, Opcode_3_0[1]);
  not not_7 (not_7_out, Opcode_3_0[1]);
  not not_8 (not_8_out, ZF);
  not not_9 (not_9_out, SF);
  and and_1 (and_1_out, not_1_out, not_2_out);
  and and_2 (Imm_Sel, Opcode_3_0[2], not_3_out);
  and and_3 (and_3_out, not_4_out, Opcode_3_0[3]);
  and and_4 (and_4_out, not_5_out, not_6_out);
  and and_5 (and_5_out, Opcode_3_0[0], not_7_out, not_8_out, not_9_out);
  or or_1 (or_1_out, and_4_out, and_5_out);
  or or_2 (REG_EN, and_1_out, Imm_Sel);
  and and_6 (Jmp_Sel, and_3_out, or_1_out);

  assign Op_1_0 = Opcode_3_0[1:0];
endmodule
