// Digital circuit 3_Bit_PC_Adder.dig as structural Verilog
module _3_Bit_PC_Adder (
  input  [2:0] I_2_0,
  output [2:0] O_2_0
);

  wire fa_2_co, fa_3_co;

  FA fa_1 (.A(I_2_0[2]), .B(1'b0), .S(O_2_0[2]), .Ci(fa_2_co));  // open: Co
  FA fa_2 (.A(I_2_0[1]), .B(1'b0), .S(O_2_0[1]), .Ci(fa_3_co), .Co(fa_2_co));
  FA fa_3 (.A(I_2_0[0]), .B(1'b1), .S(O_2_0[0]), .Ci(1'b0), .Co(fa_3_co));

  // Other names for the same wires on the sheet: A0 = I_2_0[0]; A1 = I_2_0[1]; A2 = I_2_0[2]; S0 = O_2_0[0];
  //   S1 = O_2_0[1]; S2 = O_2_0[2]
endmodule
