// Digital circuit 4x6_Bit_Reg_Set.dig as structural Verilog
module _4x6_Bit_Reg_Set (
  input  [1:0] WR_1_0,
  input  [5:0] Wrd_5_0,
  input  Clock,
  input  [1:0] Ra_1_0,
  input  [1:0] Rb_1_0,
  input  REG_EN,
  output [5:0] A_5_0,
  output [5:0] B_5_0
);

  wire A0, A1, A2, A3, reg0, reg1, reg2, reg3;
  wire [5:0] R0, R1, R2, R3;

  and and_1 (reg0, A0, REG_EN);
  and and_2 (reg1, A1, REG_EN);
  and and_3 (reg2, A2, REG_EN);
  and and_4 (reg3, A3, REG_EN);
  Decoder #(.Selector_Bits(2)) decoder_1 (.sel(WR_1_0), .out_0(A0), .out_1(A1), .out_2(A2), .out_3(A3));
  _6_Bit_Reg _6_bit_reg_1 (.Din_5_0(Wrd_5_0), .Sel(reg0), .Clock(Clock), .Dout_5_0(R0));
  _6_Bit_Reg _6_bit_reg_2 (.Din_5_0(Wrd_5_0), .Sel(reg1), .Clock(Clock), .Dout_5_0(R1));
  _6_Bit_Reg _6_bit_reg_3 (.Din_5_0(Wrd_5_0), .Sel(reg2), .Clock(Clock), .Dout_5_0(R2));
  _6_Bit_Reg _6_bit_reg_4 (.Din_5_0(Wrd_5_0), .Sel(reg3), .Clock(Clock), .Dout_5_0(R3));
  Multiplexer #(.Selector_Bits(2), .Bits(6)) multiplexer_1 (
    .sel(Ra_1_0), .in_0(R0), .in_1(R1), .in_2(R2), .in_3(R3), .out(A_5_0));
  Multiplexer #(.Selector_Bits(2), .Bits(6)) multiplexer_2 (
    .sel(Rb_1_0), .in_0(R0), .in_1(R1), .in_2(R2), .in_3(R3), .out(B_5_0));
endmodule
