// Digital circuit 6_Bit_ALU.dig as structural Verilog
module _6_Bit_ALU (
  input  [5:0] A_5_0,
  input  [5:0] B_5_0,
  input  [1:0] OP_1_0,
  output [5:0] R_5_0
);

  wire [5:0] O1, O2, O3;

  _6_Bit_OR _6_bit_or_1 (.A_5_0(A_5_0), .B_5_0(B_5_0), .R_5_0(O1));
  _6_Bit_Adder _6_bit_adder_1 (.A_5_0(A_5_0), .B_5_0(B_5_0), .R_5_0(O2));  // open: Co
  _6_Bit_ROL _6_bit_rol_1 (.A_5_0(A_5_0), .B_5_0(B_5_0), .R_5_0(O3));
  Multiplexer #(.Selector_Bits(2), .Bits(6)) multiplexer_1 (
    .sel(OP_1_0), .in_0(O1), .in_1(O2), .in_2(O3), .in_3({6{1'b0}}), .out(R_5_0));

  // Other names for the same wires on the sheet: A[5:0] = A_5_0; B[5:0] = B_5_0
endmodule
