// Digital circuit 6_Bit_Adder.dig as structural Verilog
module _6_Bit_Adder (
  input  [5:0] A_5_0,
  input  [5:0] B_5_0,
  output Co,
  output [5:0] R_5_0
);

  wire fa_2_co, fa_3_co, fa_4_co, fa_5_co, fa_6_co;

  FA fa_1 (.A(A_5_0[5]), .B(B_5_0[5]), .S(R_5_0[5]), .Ci(fa_2_co), .Co(Co));
  FA fa_2 (.A(A_5_0[4]), .B(B_5_0[4]), .S(R_5_0[4]), .Ci(fa_3_co), .Co(fa_2_co));
  FA fa_3 (.A(A_5_0[3]), .B(B_5_0[3]), .S(R_5_0[3]), .Ci(fa_4_co), .Co(fa_3_co));
  FA fa_4 (.A(A_5_0[2]), .B(B_5_0[2]), .S(R_5_0[2]), .Ci(fa_5_co), .Co(fa_4_co));
  FA fa_5 (.A(A_5_0[1]), .B(B_5_0[1]), .S(R_5_0[1]), .Ci(fa_6_co), .Co(fa_5_co));
  FA fa_6 (.A(A_5_0[0]), .B(B_5_0[0]), .S(R_5_0[0]), .Ci(1'b0), .Co(fa_6_co));

  // Other names for the same wires on the sheet: A0 = A_5_0[0]; A1 = A_5_0[1]; A2 = A_5_0[2]; A3 = A_5_0[3];
  //   A4 = A_5_0[4]; A5 = A_5_0[5]; B0 = B_5_0[0]; B1 = B_5_0[1]; B2 = B_5_0[2]; B3 = B_5_0[3]; B4 = B_5_0[4];
  //   B5 = B_5_0[5]; S0 = R_5_0[0]; S1 = R_5_0[1]; S2 = R_5_0[2]; S3 = R_5_0[3]; S4 = R_5_0[4]; S5 = R_5_0[5]
endmodule
