// Digital circuit 6_Bit_OR.dig as structural Verilog
module _6_Bit_OR (
  input  [5:0] A_5_0,
  input  [5:0] B_5_0,
  output [5:0] R_5_0
);

  or or_1 (R_5_0[0], A_5_0[0], B_5_0[0]);
  or or_2 (R_5_0[1], A_5_0[1], B_5_0[1]);
  or or_3 (R_5_0[2], A_5_0[2], B_5_0[2]);
  or or_4 (R_5_0[3], A_5_0[3], B_5_0[3]);
  or or_5 (R_5_0[4], A_5_0[4], B_5_0[4]);
  or or_6 (R_5_0[5], A_5_0[5], B_5_0[5]);

  // Other names for the same wires on the sheet: A0 = A_5_0[0]; A1 = A_5_0[1]; A2 = A_5_0[2]; A3 = A_5_0[3];
  //   A4 = A_5_0[4]; A5 = A_5_0[5]; B0 = B_5_0[0]; B1 = B_5_0[1]; B2 = B_5_0[2]; B3 = B_5_0[3]; B4 = B_5_0[4];
  //   B5 = B_5_0[5]; O0 = R_5_0[0]; O1 = R_5_0[1]; O2 = R_5_0[2]; O3 = R_5_0[3]; O4 = R_5_0[4]; O5 = R_5_0[5]
endmodule
