// Digital circuit 6_Bit_ROL.dig as structural Verilog
module _6_Bit_ROL (
  input  [5:0] A_5_0,
  input  [5:0] B_5_0,
  output [5:0] R_5_0
);

  wire and_1_out, O0, O1, O2, O3, O4, O5, or_1_out, or_2_out;

  Multiplexer #(.Selector_Bits(3)) multiplexer_1 (
    .sel(B_5_0[2:0]), .in_0(A_5_0[5]), .in_1(A_5_0[4]), .in_2(A_5_0[3]), .in_3(A_5_0[2]), .in_4(A_5_0[1]),
    .in_5(A_5_0[0]), .in_6(1'b0), .in_7(1'b0), .out(O5));
  Multiplexer #(.Selector_Bits(3)) multiplexer_2 (
    .sel(B_5_0[2:0]), .in_0(A_5_0[4]), .in_1(A_5_0[3]), .in_2(A_5_0[2]), .in_3(A_5_0[1]), .in_4(A_5_0[0]),
    .in_5(A_5_0[5]), .in_6(1'b0), .in_7(1'b0), .out(O4));
  Multiplexer #(.Selector_Bits(3)) multiplexer_3 (
    .sel(B_5_0[2:0]), .in_0(A_5_0[3]), .in_1(A_5_0[2]), .in_2(A_5_0[1]), .in_3(A_5_0[0]), .in_4(A_5_0[5]),
    .in_5(A_5_0[4]), .in_6(1'b0), .in_7(1'b0), .out(O3));
  Multiplexer #(.Selector_Bits(3)) multiplexer_4 (
    .sel(B_5_0[2:0]), .in_0(A_5_0[2]), .in_1(A_5_0[1]), .in_2(A_5_0[0]), .in_3(A_5_0[5]), .in_4(A_5_0[4]),
    .in_5(A_5_0[3]), .in_6(1'b0), .in_7(1'b0), .out(O2));
  Multiplexer #(.Selector_Bits(3)) multiplexer_5 (
    .sel(B_5_0[2:0]), .in_0(A_5_0[1]), .in_1(A_5_0[0]), .in_2(A_5_0[5]), .in_3(A_5_0[4]), .in_4(A_5_0[3]),
    .in_5(A_5_0[2]), .in_6(1'b0), .in_7(1'b0), .out(O1));
  Multiplexer #(.Selector_Bits(3)) multiplexer_6 (
    .sel(B_5_0[2:0]), .in_0(A_5_0[0]), .in_1(A_5_0[5]), .in_2(A_5_0[4]), .in_3(A_5_0[3]), .in_4(A_5_0[2]),
    .in_5(A_5_0[1]), .in_6(1'b0), .in_7(1'b0), .out(O0));
  or or_1 (or_1_out, B_5_0[5], B_5_0[4], B_5_0[3]);
  and and_1 (and_1_out, B_5_0[2], B_5_0[1]);
  or or_2 (or_2_out, or_1_out, and_1_out);
  Multiplexer #(.Bits(6)) multiplexer_7 (
    .sel(or_2_out), .in_0({O5, O4, O3, O2, O1, O0}), .in_1({6{1'b0}}), .out(R_5_0));

  // Other names for the same wires on the sheet: A0 = A_5_0[0]; A1 = A_5_0[1]; A2 = A_5_0[2]; A3 = A_5_0[3];
  //   A4 = A_5_0[4]; A5 = A_5_0[5]; B0 = B_5_0[0]; B1 = B_5_0[1]; B2 = B_5_0[2]; B3 = B_5_0[3]; B4 = B_5_0[4];
  //   B5 = B_5_0[5]
endmodule
