// Digital circuit 6_Bit_Reg.dig as structural Verilog
module _6_Bit_Reg (
  input  [5:0] Din_5_0,
  input  Sel,
  input  Clock,
  output [5:0] Dout_5_0
);

  _1_Bit_Reg _1_bit_reg_1 (.Din(Din_5_0[0]), .Sel(Sel), .Clock(Clock), .Dout(Dout_5_0[0]));
  _1_Bit_Reg _1_bit_reg_2 (.Din(Din_5_0[1]), .Sel(Sel), .Clock(Clock), .Dout(Dout_5_0[1]));
  _1_Bit_Reg _1_bit_reg_3 (.Din(Din_5_0[2]), .Sel(Sel), .Clock(Clock), .Dout(Dout_5_0[2]));
  _1_Bit_Reg _1_bit_reg_4 (.Din(Din_5_0[3]), .Sel(Sel), .Clock(Clock), .Dout(Dout_5_0[3]));
  _1_Bit_Reg _1_bit_reg_5 (.Din(Din_5_0[4]), .Sel(Sel), .Clock(Clock), .Dout(Dout_5_0[4]));
  _1_Bit_Reg _1_bit_reg_6 (.Din(Din_5_0[5]), .Sel(Sel), .Clock(Clock), .Dout(Dout_5_0[5]));

  // Other names for the same wires on the sheet: clk = Clock; D0 = Dout_5_0[0]; D1 = Dout_5_0[1]; D2 = Dout_5_0[2];
  //   D3 = Dout_5_0[3]; D4 = Dout_5_0[4]; D5 = Dout_5_0[5]; d0_t = Din_5_0[0]; d1_t = Din_5_0[1]; d2_t = Din_5_0[2];
  //   d3_t = Din_5_0[3]; d4_t = Din_5_0[4]; d5_t = Din_5_0[5]
endmodule
