// Digital circuit 7x17_SRAM_Set.dig as structural Verilog
module _7x17_SRAM_Set (
  input  [2:0] RA1_2_0,
  input  [2:0] RA2_2_0,
  input  [2:0] WA_2_0,
  input  Clock,
  input  [16:0] WD_16_0,
  input  WE,
  output [16:0] RD1_16_0,
  output [16:0] RD2_16_0
);

  wire A0, A1, A2, A3, A4, A5, A6, R1_0, R1_1, R1_2, R1_3, R1_4, R1_5, R1_6, R2_0, R2_1, R2_2, R2_3, R2_4,
       R2_5, R2_6, W0, W1, W2, W3, W4, W5, W6;
  wire [16:0] RD1_0, RD1_1, RD1_2, RD1_3, RD1_4, RD1_5, RD1_6, RD2_0, RD2_1, RD2_2, RD2_3, RD2_4, RD2_5,
       RD2_6;

  Decoder #(.Selector_Bits(3)) decoder_1 (
    .sel(RA1_2_0), .out_0(R1_0), .out_1(R1_1), .out_2(R1_2), .out_3(R1_3), .out_4(R1_4), .out_5(R1_5),
    .out_6(R1_6));  // open: out_7
  Decoder #(.Selector_Bits(3)) decoder_2 (
    .sel(RA2_2_0), .out_0(R2_0), .out_1(R2_1), .out_2(R2_2), .out_3(R2_3), .out_4(R2_4), .out_5(R2_5),
    .out_6(R2_6));  // open: out_7
  Decoder #(.Selector_Bits(3)) decoder_3 (
    .sel(WA_2_0), .out_0(A0), .out_1(A1), .out_2(A2), .out_3(A3), .out_4(A4), .out_5(A5), .out_6(A6));  // open: out_7
  and and_1 (W0, A0, WE);
  and and_2 (W1, A1, WE);
  and and_3 (W2, A2, WE);
  and and_4 (W3, A3, WE);
  and and_5 (W4, A4, WE);
  and and_6 (W5, A5, WE);
  and and_7 (W6, A6, WE);
  _1x17_SRAM _1x17_sram_1 (.RS1(R1_0), .RS2(R2_0), .WS(W0), .WD_16_0(WD_16_0), .Clock(Clock), .RD1(RD1_0), .RD2(RD2_0));
  _1x17_SRAM _1x17_sram_2 (.RS1(R1_1), .RS2(R2_1), .WS(W1), .WD_16_0(WD_16_0), .Clock(Clock), .RD1(RD1_1), .RD2(RD2_1));
  _1x17_SRAM _1x17_sram_3 (.RS1(R1_2), .RS2(R2_2), .WS(W2), .WD_16_0(WD_16_0), .Clock(Clock), .RD1(RD1_2), .RD2(RD2_2));
  _1x17_SRAM _1x17_sram_4 (.RS1(R1_3), .RS2(R2_3), .WS(W3), .WD_16_0(WD_16_0), .Clock(Clock), .RD1(RD1_3), .RD2(RD2_3));
  _1x17_SRAM _1x17_sram_5 (.RS1(R1_4), .RS2(R2_4), .WS(W4), .WD_16_0(WD_16_0), .Clock(Clock), .RD1(RD1_4), .RD2(RD2_4));
  _1x17_SRAM _1x17_sram_6 (.RS1(R1_5), .RS2(R2_5), .WS(W5), .WD_16_0(WD_16_0), .Clock(Clock), .RD1(RD1_5), .RD2(RD2_5));
  _1x17_SRAM _1x17_sram_7 (.RS1(R1_6), .RS2(R2_6), .WS(W6), .WD_16_0(WD_16_0), .Clock(Clock), .RD1(RD1_6), .RD2(RD2_6));
  assign RD1_16_0 = RD1_0 | RD1_1 | RD1_2 | RD1_3 | RD1_4 | RD1_5 | RD1_6;  // Or or_1, 17 bits wide
  assign RD2_16_0 = RD2_0 | RD2_1 | RD2_2 | RD2_3 | RD2_4 | RD2_5 | RD2_6;  // Or or_2, 17 bits wide

  // Other names for the same wires on the sheet: clk = Clock; wd[16:0] = WD_16_0
endmodule
