// Digital circuit FA.dig as structural Verilog
module FA (
  input  A,
  input  Ci,
  input  B,
  output S,
  output Co
);

  wire ha_1_co, ha_1_s, ha_2_co;

  HA ha_1 (.A(A), .B(B), .S(ha_1_s), .Co(ha_1_co));
  HA ha_2 (.A(ha_1_s), .B(Ci), .S(S), .Co(ha_2_co));
  or or_1 (Co, ha_2_co, ha_1_co);
endmodule
