// Digital circuit ISA+CPU.dig as structural Verilog
module ISA_CPU (
  input  [2:0] WA_2_0,
  input  [16:0] WD_16_0,
  input  WE,
  input  CLOCK,
  input  PC_EN,
  input  [2:0] RA2_2_0,
  input  ZF,
  input  SF,
  output [16:0] RD2_16_0,
  output [5:0] A_5_0,
  output [1:0] R2_1_0,
  output [1:0] WR_1_0,
  output [5:0] B_5_0,
  output [5:0] R_5_0,
  output [1:0] R1_1_0,
  output [1:0] OP
);

  wire CPU_CLK, Imm_Sel, Jmp_Sel, reg_en;
  wire [2:0] _3_bit_pc_adder_1_o_2_0, _3_bit_program_counter_1_o_2_0, multiplexer_1_out;
  wire [3:0] Imm_Val;
  wire [4:0] Unused;
  wire [5:0] _4x6_bit_reg_set_1_b_5_0;
  wire [16:13] _7x17_sram_set_1_rd1_16_0;

  Multiplexer #(.Bits(3)) multiplexer_1 (
    .sel(Jmp_Sel), .in_0(_3_bit_pc_adder_1_o_2_0), .in_1({R1_1_0, R2_1_0[1]}), .out(multiplexer_1_out));
  _3_Bit_PC_Adder _3_bit_pc_adder_1 (.I_2_0(_3_bit_program_counter_1_o_2_0), .O_2_0(_3_bit_pc_adder_1_o_2_0));
  _3_Bit_Program_Counter _3_bit_program_counter_1 (
    .I_2_0(multiplexer_1_out), .CLK(CPU_CLK), .O_2_0(_3_bit_program_counter_1_o_2_0));
  and and_1 (CPU_CLK, PC_EN, CLOCK);
  _7x17_SRAM_Set _7x17_sram_set_1 (
    .RA1_2_0(_3_bit_program_counter_1_o_2_0), .RA2_2_0(RA2_2_0), .WA_2_0(WA_2_0), .WD_16_0(WD_16_0), .WE(WE),
    .Clock(CLOCK), .RD1_16_0({_7x17_sram_set_1_rd1_16_0, R1_1_0, R2_1_0, Imm_Val, Unused}),
    .RD2_16_0(RD2_16_0));
  _3_Bit_Control_Unit _3_bit_control_unit_1 (
    .Opcode_3_0(_7x17_sram_set_1_rd1_16_0), .ZF(ZF), .SF(SF), .Op_1_0(OP), .REG_EN(reg_en),
    .Imm_Sel(Imm_Sel), .Jmp_Sel(Jmp_Sel));
  _4x6_Bit_Reg_Set _4x6_bit_reg_set_1 (
    .WR_1_0(R1_1_0), .Clock(CPU_CLK), .REG_EN(reg_en), .Wrd_5_0(R_5_0), .A_5_0(A_5_0),
    .B_5_0(_4x6_bit_reg_set_1_b_5_0), .Ra_1_0(R1_1_0), .Rb_1_0(R2_1_0));
  _6_Bit_ALU _6_bit_alu_1 (.A_5_0(A_5_0), .B_5_0(B_5_0), .OP_1_0(OP), .R_5_0(R_5_0));
  Multiplexer #(.Bits(6)) multiplexer_2 (
    .sel(Imm_Sel), .in_0(_4x6_bit_reg_set_1_b_5_0), .in_1({R2_1_0, Imm_Val}), .out(B_5_0));

  assign WR_1_0 = R1_1_0;

  // Other names for the same wires on the sheet: R2[1:0] = R2_1_0; JMP_ADDR[2:0] = {R1_1_0, R2_1_0[1]};
  //   R1[1:0] = R1_1_0; wr[1:0] = R1_1_0; a[5:0] = A_5_0; b[5:0] = B_5_0; clk = CLOCK; r[5:0] = R_5_0;
  //   rd2[16:0] = RD2_16_0

  // Notes on the sheet:
  //   ISA = Opcode + Operands
  //   Register Mode (Type of Op = 00) =  2Bit(Type of Operation) + 2Bit(OP) + 2Bit(Reg1) + 2Bit(Reg2) + 9Bit(Unused) 
  //   Immediate  Mode (Type of Op = 01) =  2Bit(Type of Operation) + 2Bit(OP) + 2Bit(Reg1) + 6Bit(Imm Value) + 5Bit(Unused)
  //   Jump Mode (Type of Op = 10) = 2Bit(Type of Operation) + 2Bit(OP)  + 3Bit(Address of Reg) + 10Bit(Unused)
  //   OR(Op = 00), ADD(Op = 01) , ROL(Op = 10) 
  //   JMP(Op = 00), JG(Op = 01) 
  //           JMP-JG:     ADD R1,5 -> 0b01010100010100000 (Immediate Mode)
  //          JMP-TO:     ADD R2,3 -> 0b01011000001100000 (Immediate Mode)
  //                      JMP JMP-TO -> 0b10000010000000000 (Jump Mode: JMPLABEL)
  //                      JG JMP-JG ->  0b10010000000000000 (Jump Mode: JG LABEL)
  //                      OR R1,R2 -> 0b00000110000000000 (Register Mode)
  //                      ROL R1, 1 ->  0b01100100000100000 (Immediate Mode)
endmodule
